// Logisim project Assignment_4.circ as structural Verilog: 1 circuit, main circuit main
module main (
  input  A,
  input  B,
  input  A_2,
  input  B_2,
  input  B_3,
  input  C,
  input  A_3,
  input  B_4,
  input  C_2,
  input  A_4,
  output DIFFERENCE,
  output BORROW,
  output SUM,
  output CARRY,
  output SUM_2,
  output CARRY_2,
  output DIFFERENCE_2,
  output BORROW_2
);

  wire and_3_out, and_4_out, and_5_out, and_6_out, not_1_out, not_2_out, xor_3_out, xor_4_out;

  not not_1 (not_1_out, A);
  not not_2 (not_2_out, A_4);
  xor xor_1 (DIFFERENCE, A, B);
  and and_1 (BORROW, not_1_out, B);
  xor xor_2 (SUM, A_2, B_2);
  and and_2 (CARRY, A_2, B_2);
  xor xor_3 (xor_3_out, B_3, C);
  and and_3 (and_3_out, xor_3_out, A_3);
  and and_4 (and_4_out, B_3, C);
  xor xor_4 (xor_4_out, B_4, C_2);
  and and_5 (and_5_out, xor_4_out, not_2_out);
  and and_6 (and_6_out, B_4, C_2);
  xor xor_5 (SUM_2, xor_3_out, A_3);
  or or_1 (CARRY_2, and_3_out, and_4_out);
  xor xor_6 (DIFFERENCE_2, xor_4_out, A_4);
  or or_2 (BORROW_2, and_5_out, and_6_out);

  // Notes on the sheet:
  //   HALF SUBTRACTOR
  //   HALF ADDER
  //   FULL ADDER
  //   FULL SUBTRACTOR
endmodule
