// Logisim project Assignment_5.circ as structural Verilog: 1 circuit, main circuit main
module main (
  input  A,
  input  B,
  input  C,
  input  A7,
  input  B7,
  input  A6,
  input  B6,
  input  A5,
  input  B5,
  input  A4,
  input  B4,
  input  A3,
  input  B3,
  input  A2,
  input  B2,
  input  A1,
  input  B1,
  input  A0,
  input  B0,
  input  SELECT,
  input  I1,
  input  I2,
  input  in_23,
  input  in_24,
  input  in_25,
  input  [7:0] in_26,
  input  in_27,
  input  in_28,
  input  in_29,
  input  in_30,
  input  in_31,
  input  S2,
  input  S1,
  input  S0,
  input  S1_2,
  input  S0_2,
  input  C_2,
  input  B_2,
  input  A_2,
  input  S0_3,
  input  S1_3,
  output out_42,
  output out_43,
  output out_44,
  output out_45,
  output out_46,
  output out_47,
  output out_48,
  output out_49,
  output out_50,
  output out_51,
  output Comparator_O_P,
  output Output,
  output out_54,
  output out_55,
  output out_56,
  output out_57,
  output out_58,
  output out_59,
  output out_60,
  output out_61,
  output out_62,
  output out_63,
  output out_64
);

  wire A_out, and_2_out, and_3_out, and_4_out, and_5_out, and_10_out, and_11_out, and_12_out, and_13_out,
       and_14_out, and_15_out, and_17_out, and_18_out, and_19_out, and_20_out, and_21_out, and_22_out,
       and_23_out, and_25_out, and_26_out, and_27_out, and_28_out, and_29_out, and_30_out, and_31_out,
       and_32_out, and_33_out, and_34_out, and_35_out, and_36_out, and_39_out, and_40_out, and_41_out,
       and_44_out, and_45_out, and_46_out, and_52_out, and_53_out, B_out, C_out, I0_out, I1_out, I2_out,
       I3_out, I4_out, I5_out, I6_out, I7_out, I_out, not_1_out, not_2_out, not_3_out, not_4_out, not_5_out,
       not_6_out, not_7_out, not_8_out, not_9_out, not_10_out, not_11_out, or_6_out, xnor_1_out, xnor_2_out,
       xnor_3_out, xnor_4_out, xnor_5_out, xnor_6_out, xnor_7_out, xnor_8_out, xnor_9_out, xor_1_out,
       xor_2_out, xor_3_out;

  and and_1 (out_44, A, B, C);
  and and_2 (and_2_out, in_23, in_24);
  and and_3 (and_3_out, in_25, in_27);
  and and_4 (and_4_out, in_28, in_29);
  and and_5 (and_5_out, in_30, in_31);
  Button I7 (.out(I7_out));
  not not_1 (not_1_out, S1_3);
  not not_2 (not_2_out, S0_3);
  and and_6 (out_46, A, not_6_out, C);
  and and_7 (out_45, A, B, not_8_out);
  and and_8 (out_54, and_2_out, and_3_out);
  and and_9 (out_57, and_4_out, and_5_out);
  and and_10 (and_10_out, S2, S1, S0);
  Button I6 (.out(I6_out));
  and and_11 (and_11_out, I6_out, and_18_out);
  and and_12 (and_12_out, I7_out, and_10_out);
  not not_3 (not_3_out, S0_2);
  not not_4 (not_4_out, S1_2);
  Button I (.out(I_out));
  and and_13 (and_13_out, S1_3, S0_3);
  and and_14 (and_14_out, not_2_out, not_1_out);
  and and_15 (and_15_out, and_14_out, xor_3_out);
  Button u_B (.out(B_out));
  Button u_A (.out(A_out));
  or or_1 (out_42, A_out, B_out);
  and and_16 (out_47, A, not_8_out, not_6_out);
  not not_5 (not_5_out, SELECT);
  and and_17 (and_17_out, S2, not_10_out, S0);
  and and_18 (and_18_out, S2, S1, not_11_out);
  Button I5 (.out(I5_out));
  and and_19 (and_19_out, I5_out, and_17_out);
  xor xor_1 (xor_1_out, A_2, and_13_out);
  and and_20 (and_20_out, S0_3, not_1_out);
  and and_21 (and_21_out, S1_3, not_2_out);
  and and_22 (and_22_out, and_20_out, xnor_9_out);
  and and_23 (and_23_out, and_21_out, xor_3_out);
  or or_2 (out_63, and_15_out, and_22_out, and_23_out, and_36_out);
  Button D ();  // open: out
  Button u_C (.out(C_out));
  or or_3 (out_43, C_out, A_out);
  not not_6 (not_6_out, B);
  not not_7 (not_7_out, A);
  and and_24 (out_48, C, B, not_7_out);
  and and_25 (and_25_out, SELECT, I1);
  and and_26 (and_26_out, I2, not_5_out);
  and and_27 (and_27_out, S2, not_11_out, not_10_out);
  Button I3 (.out(I3_out));
  Button I4 (.out(I4_out));
  and and_28 (and_28_out, I4_out, and_27_out);
  or or_4 (out_58, and_12_out, and_11_out, and_19_out, and_28_out, and_40_out, and_41_out, and_46_out, and_53_out);
  and and_29 (and_29_out, S0_2, S1_2);
  and and_30 (and_30_out, S1_2, not_3_out);
  and and_31 (and_31_out, not_4_out, S0_2);
  and and_32 (and_32_out, not_3_out, not_4_out);
  and and_33 (and_33_out, xor_2_out, xor_1_out);
  and and_34 (and_34_out, C_2, B_2);
  and and_35 (and_35_out, S0_3, S1_3);
  and and_36 (and_36_out, and_35_out, xor_3_out);
  not not_8 (not_8_out, C);
  and and_37 (out_49, not_7_out, B, not_8_out);
  and and_38 (out_50, not_7_out, not_6_out, C);
  xnor xnor_1 (xnor_1_out, A7, B7);
  xnor xnor_2 (xnor_2_out, A6, B6);
  xnor xnor_3 (xnor_3_out, A5, B5);
  xnor xnor_4 (xnor_4_out, A4, B4);
  xnor xnor_5 (xnor_5_out, A3, B3);
  xnor xnor_6 (xnor_6_out, A2, B2);
  xnor xnor_7 (xnor_7_out, A1, B1);
  xnor xnor_8 (xnor_8_out, A0, B0);
  or or_5 (Output, and_25_out, and_26_out);
  not not_9 (not_9_out, S2);
  not not_10 (not_10_out, S1);
  and and_39 (and_39_out, S0, S1, not_9_out);
  Button u_I2 (.out(I2_out));
  and and_40 (and_40_out, I3_out, and_39_out);
  and and_41 (and_41_out, I2_out, and_44_out);
  xor xor_2 (xor_2_out, C_2, B_2);
  and and_42 (out_64, S1_3, or_6_out);
  and and_43 (out_51, not_7_out, not_6_out, not_8_out);
  not not_11 (not_11_out, S0);
  and and_44 (and_44_out, not_9_out, S1, not_11_out);
  and and_45 (and_45_out, not_9_out, not_10_out, S0);
  Button u_I1 (.out(I1_out));
  and and_46 (and_46_out, I1_out, and_45_out);
  and and_47 (out_59, and_29_out, I_out);
  and and_48 (out_60, and_30_out, I_out);
  and and_49 (out_61, and_31_out, I_out);
  and and_50 (out_62, and_32_out, I_out);
  xor xor_3 (xor_3_out, xor_2_out, A_2);
  or or_6 (or_6_out, and_33_out, and_34_out);
  and and_51 (Comparator_O_P, xnor_1_out, xnor_2_out, xnor_3_out, xnor_4_out, xnor_5_out, xnor_6_out, xnor_7_out, xnor_8_out);
  and and_52 (and_52_out, not_9_out, not_10_out, not_11_out);
  Button I0 (.out(I0_out));
  and and_53 (and_53_out, I0_out, and_52_out);
  NotExactlyOne xnor_9 (.out(xnor_9_out), .in0(A_2), .in1(C_2), .in2(B_2));
  and and_54 (out_55, in_26[0], in_26[1], in_26[2], in_26[3]);
  and and_55 (out_56, in_26[4], in_26[5], in_26[6], in_26[7]);

  // Notes on the sheet:
  //   4 - 2 Decoder 
  //   3 - 8 Decoder
  //   2 : 1 Multiplexer
  //   8 Bit Comparator
  //   Question 5
  //   8: 1 Multiplexer
  //   1 : 4 Demultiplexer
  //   Question 8
endmodule
