// Logisim project Assignment_6.circ as structural Verilog: 2 circuits, main circuit main
module main (
  input  _4_Bit_Full_Adder,
  input  in_2,
  input  in_3,
  input  in_4,
  input  in_5,
  input  in_6,
  input  in_7,
  input  in_8,
  input  in_9,
  input  _4_Bit_Subtractor,
  input  in_11,
  input  in_12,
  input  in_13,
  input  in_14,
  input  in_15,
  input  in_16,
  input  in_17,
  input  in_18,
  input  B3,
  input  B2,
  input  B1,
  input  B0,
  input  A0,
  input  A1,
  input  A2,
  input  in_26,
  input  A3,
  input  in_28,
  input  in_29,
  input  in_30,
  input  in_31,
  input  in_32,
  input  in_33,
  input  in_34,
  input  in_35,
  input  in_36,
  input  B3_2,
  input  A3_2,
  input  [3:0] Dividend,
  input  [3:0] Divisor,
  input  A2_2,
  input  A1_2,
  input  A0_2,
  input  B2_2,
  input  B1_2,
  input  B0_2,
  output C4,
  output C3,
  output C2,
  output C1,
  output C0,
  output C3_2,
  output C2_2,
  output C1_2,
  output C0_2,
  output C7,
  output C6,
  output C5,
  output C4_2,
  output C3_3,
  output C2_3,
  output C1_3,
  output C0_3,
  output out_64,
  output out_65,
  output out_66,
  output out_67,
  output out_68,
  output out_69,
  output out_70,
  output D3,
  output [3:0] out_72,
  output D2,
  output [3:0] out_74,
  output D1,
  output D0,
  output R3,
  output R2,
  output R1,
  output R0
);

  wire and_21_out, and_22_out, and_23_out, and_24_out, and_25_out, and_26_out, and_27_out, and_28_out,
       and_29_out, and_30_out, and_31_out, and_32_out, and_33_out, and_34_out, and_35_out, and_36_out,
       and_37_out, and_38_out, and_39_out, and_40_out, and_41_out, and_42_out, and_43_out, and_44_out,
       and_45_out, and_46_out, and_47_out, and_48_out, and_49_out, and_51_out, and_52_out, and_53_out,
       and_54_out, and_55_out, and_56_out, and_57_out, and_58_out, and_59_out, and_60_out, and_61_out,
       and_62_out, and_63_out, and_64_out, and_65_out, and_66_out, not_1_out, not_2_out, not_3_out,
       not_4_out, not_5_out, not_6_out, not_7_out, not_8_out, not_9_out, not_10_out, not_11_out, not_12_out,
       not_13_out, not_14_out, not_15_out, not_16_out, not_17_out, not_18_out, not_19_out, not_20_out,
       not_21_out, not_22_out, not_23_out, not_24_out, not_25_out, not_26_out, not_27_out, not_28_out,
       not_29_out, not_30_out, not_31_out, not_32_out, not_33_out, not_34_out, not_35_out, not_36_out,
       not_37_out, not_38_out, not_39_out, not_40_out, not_41_out, not_42_out, not_43_out, not_44_out,
       not_45_out, not_46_out, not_47_out, not_48_out, not_49_out, or_6_out, or_7_out, or_8_out, or_9_out,
       or_10_out, or_12_out, or_13_out, xor_2_out, xor_3_out, xor_4_out, xor_5_out, xor_7_out, xor_8_out,
       xor_9_out, xor_10_out, xor_11_out, xor_12_out, xor_13_out, xor_14_out, xor_16_out, xor_17_out,
       xor_21_out, xor_22_out;
  wire [1:0] and_50_out;
  wire [2:0] adder_4_cout, and_11_out, and_15_out, and_17_out, and_70_out;
  wire [3:0] adder_3_cout, adder_5_cout, and_6_out, and_18_out;

  and and_1 (B3, A2, B3);
  and and_2 (and_6_out[3], A3, B3);
  xor xor_1 (out_64, in_32, in_28);
  and and_3 (and_11_out[2], A2, B2);
  and and_4 (and_6_out[2], A3, B2);
  and and_5 (and_11_out[1], A2, B1);
  and and_6 (and_6_out[0], A3, B0);
  and and_7 (and_6_out[1], A3, B1);
  and and_8 (and_15_out[2], in_29, in_33);
  xor xor_2 (xor_2_out, _4_Bit_Subtractor, in_16);
  xor xor_3 (xor_3_out, _4_Bit_Subtractor, in_15);
  and and_9 (and_18_out[3], A1, B3);
  and and_10 (and_18_out[2], A1, B2);
  and and_11 (and_11_out[0], A2, B0);
  and and_12 (and_17_out[2], in_30, in_33);
  and and_13 (and_17_out[1], in_30, in_34);
  and and_14 (and_15_out[1], in_29, in_34);
  and and_15 (and_15_out[0], in_29, in_35);
  xor xor_4 (xor_4_out, in_18, _4_Bit_Subtractor);
  xor xor_5 (xor_5_out, _4_Bit_Subtractor, in_17);
  and and_16 (and_18_out[1], A1, B1);
  and and_17 (and_17_out[0], in_30, in_35);
  not not_1 (not_1_out, B2_2);
  not not_2 (not_2_out, B1_2);
  not not_3 (not_3_out, B2_2);
  not not_4 (not_4_out, B1_2);
  not not_5 (not_5_out, B2_2);
  not not_6 (not_6_out, B0_2);
  not not_7 (not_7_out, B2_2);
  not not_8 (not_8_out, B2_2);
  not not_9 (not_9_out, B1_2);
  not not_10 (not_10_out, B2_2);
  not not_11 (not_11_out, B0_2);
  not not_12 (not_12_out, A2_2);
  not not_13 (not_13_out, B2_2);
  not not_14 (not_14_out, A1_2);
  not not_15 (not_15_out, B2_2);
  not not_16 (not_16_out, B1_2);
  not not_17 (not_17_out, B0_2);
  not not_18 (not_18_out, B1_2);
  not not_19 (not_19_out, B1_2);
  not not_20 (not_20_out, B0_2);
  not not_21 (not_21_out, A1_2);
  not not_22 (not_22_out, A0_2);
  not not_23 (not_23_out, A1_2);
  not not_24 (not_24_out, A0_2);
  not not_25 (not_25_out, A2_2);
  not not_26 (not_26_out, A0_2);
  not not_27 (not_27_out, A2_2);
  not not_28 (not_28_out, B1_2);
  not not_29 (not_29_out, B0_2);
  not not_30 (not_30_out, A0_2);
  not not_31 (not_31_out, B1_2);
  not not_32 (not_32_out, A1_2);
  not not_33 (not_33_out, B2_2);
  not not_34 (not_34_out, A2_2);
  not not_35 (not_35_out, A1_2);
  not not_36 (not_36_out, B0_2);
  not not_37 (not_37_out, A2_2);
  not not_38 (not_38_out, A1_2);
  not not_39 (not_39_out, B0_2);
  not not_40 (not_40_out, A1_2);
  not not_41 (not_41_out, A0_2);
  not not_42 (not_42_out, B2_2);
  not not_43 (not_43_out, A0_2);
  not not_44 (not_44_out, B1_2);
  not not_45 (not_45_out, B2_2);
  and and_18 (and_18_out[0], A1, B0);
  Adder #(.width(4)) adder_1 (.a(adder_3_cout), .b(and_6_out), .out({C6, C5, C4_2, C3_3}), .cout(C7));  // open: cin
  and and_19 (and_50_out[1], in_31, in_33);
  Adder #(.width(3)) adder_2 (
    .a(adder_4_cout), .b(and_15_out), .out({out_66, out_67, out_68}), .cout(out_65));  // open: cin
  xor xor_6 (D3, A3_2, B3_2);
  and and_20 (D2, A2_2, not_1_out, not_2_out, B0_2);
  and and_21 (and_21_out, A1_2, not_3_out, not_4_out, B0_2);
  and and_22 (and_22_out, A2_2, not_5_out, B1_2, not_6_out);
  and and_23 (and_23_out, A2_2, A1_2, not_7_out, B1_2);
  and and_24 (and_24_out, A0_2, not_8_out, not_9_out, B0_2);
  and and_25 (and_25_out, A1_2, not_10_out, B1_2, not_11_out);
  and and_26 (and_26_out, not_12_out, A1_2, A0_2, not_13_out, B1_2);
  and and_27 (and_27_out, A2_2, not_14_out, not_15_out, B1_2, B0_2);
  and and_28 (and_28_out, A2_2, B2_2, not_16_out, not_17_out);
  and and_29 (and_29_out, A2_2, A0_2, B2_2, not_18_out);
  and and_30 (and_30_out, A2_2, A1_2, B2_2, not_19_out);
  and and_31 (and_31_out, A2_2, A1_2, B2_2, not_20_out);
  and and_32 (and_32_out, A2_2, A1_2, A0_2, B2_2);
  and and_33 (and_33_out, A2_2, not_21_out, not_22_out, B2_2, B0_2);
  and and_34 (and_34_out, A2_2, not_23_out, B2_2, B1_2);
  and and_35 (and_35_out, A2_2, not_24_out, B2_2, B1_2, B0_2);
  and and_36 (and_36_out, not_25_out, A1_2, not_26_out, B1_2, B0_2);
  and and_37 (and_37_out, not_27_out, A1_2, B2_2);
  and and_38 (and_38_out, A1_2, B2_2, not_28_out, not_29_out);
  and and_39 (and_39_out, A1_2, not_30_out, B2_2, B1_2, B0_2);
  and and_40 (and_40_out, A1_2, A0_2, B2_2, not_31_out);
  and and_41 (and_41_out, A2_2, not_32_out, A0_2, not_33_out, B1_2, B0_2);
  and and_42 (and_42_out, not_34_out, not_35_out, A0_2, B1_2);
  and and_43 (and_43_out, A0_2, B1_2, not_36_out);
  and and_44 (and_44_out, not_37_out, A0_2, B2_2);
  and and_45 (and_45_out, not_38_out, A0_2, B2_2);
  and and_46 (and_46_out, A0_2, B2_2, not_39_out);
  and and_47 (and_47_out, A2_2, not_40_out, not_41_out, not_42_out, B1_2, B0_2);
  and and_48 (and_48_out, A2_2, A1_2, not_43_out, B2_2, not_44_out, B0_2);
  and and_49 (and_49_out, A2_2, A1_2, A0_2, not_45_out, B1_2);
  xor xor_7 (xor_7_out, _4_Bit_Full_Adder, in_9);
  xor xor_8 (xor_8_out, or_6_out, in_8);
  xor xor_9 (xor_9_out, or_9_out, in_7);
  xor xor_10 (xor_10_out, _4_Bit_Subtractor, xor_4_out);
  xor xor_11 (xor_11_out, or_7_out, xor_5_out);
  xor xor_12 (xor_12_out, or_8_out, xor_2_out);
  xor xor_13 (xor_13_out, or_12_out, xor_3_out);
  Adder #(.width(4)) adder_3 (
    .a(adder_5_cout), .b({B3, and_11_out}), .out({adder_3_cout[2:0], C2_3}), .cout(adder_3_cout[3]));  // open: cin
  and and_50 (and_50_out[0], in_31, in_34);
  Adder #(.width(3)) adder_4 (
    .a({in_36, and_50_out}), .b(and_17_out), .out({adder_4_cout[1:0], out_69}), .cout(adder_4_cout[2]));  // open: cin
  or or_1 (D1, and_21_out, and_22_out, and_23_out);
  or or_2 (D0, and_24_out, and_25_out, and_26_out, and_27_out, and_28_out, and_29_out, and_30_out, and_31_out, and_32_out);
  or or_3 (R2, and_33_out, and_34_out, and_35_out);
  or or_4 (R1, and_36_out, and_37_out, and_38_out, and_39_out, and_40_out, and_41_out);
  or or_5 (R0, and_42_out, and_43_out, and_44_out, and_45_out, and_46_out, and_47_out, and_48_out, and_49_out);
  and and_51 (and_51_out, xor_7_out, in_5);
  and and_52 (and_52_out, in_9, _4_Bit_Full_Adder);
  and and_53 (and_53_out, xor_8_out, in_4);
  and and_54 (and_54_out, in_8, or_6_out);
  and and_55 (and_55_out, xor_9_out, in_3);
  and and_56 (and_56_out, in_7, or_9_out);
  xor xor_14 (xor_14_out, or_10_out, in_6);
  and and_57 (and_57_out, xor_14_out, in_2);
  and and_58 (and_58_out, in_6, or_10_out);
  and and_59 (and_59_out, xor_10_out, in_14);
  and and_60 (and_60_out, xor_4_out, _4_Bit_Subtractor);
  and and_61 (and_61_out, xor_11_out, in_13);
  and and_62 (and_62_out, xor_5_out, or_7_out);
  and and_63 (and_63_out, xor_12_out, in_12);
  and and_64 (and_64_out, xor_2_out, or_8_out);
  and and_65 (and_65_out, xor_13_out, in_11);
  and and_66 (and_66_out, xor_3_out, or_12_out);
  and and_67 (and_70_out[2], A0, B3);
  and and_68 (and_70_out[1], A0, B2);
  Adder #(.width(4)) adder_5 (
    .a({in_26, and_70_out}), .b(and_18_out), .out({adder_5_cout[2:0], C1_3}), .cout(adder_5_cout[3]));  // open: cin
  and and_69 (out_70, in_31, in_35);
  xor xor_15 (C0, xor_7_out, in_5);
  or or_6 (or_6_out, and_51_out, and_52_out);
  xor xor_16 (xor_16_out, xor_10_out, in_14);
  or or_7 (or_7_out, and_59_out, and_60_out);
  xor xor_17 (xor_17_out, xor_11_out, in_13);
  or or_8 (or_8_out, and_61_out, and_62_out);
  and and_70 (and_70_out[0], A0, B1);
  xor xor_18 (C1, xor_8_out, in_4);
  or or_9 (or_9_out, and_53_out, and_54_out);
  xor xor_19 (C2, xor_9_out, in_3);
  or or_10 (or_10_out, and_55_out, and_56_out);
  xor xor_20 (C3, xor_14_out, in_2);
  or or_11 (C4, and_57_out, and_58_out);
  xor xor_21 (xor_21_out, xor_12_out, in_12);
  or or_12 (or_12_out, and_63_out, and_64_out);
  xor xor_22 (xor_22_out, xor_13_out, in_11);
  or or_13 (or_13_out, and_65_out, and_66_out);
  and and_71 (C0_3, A0, B0);
  not not_46 (not_46_out, or_13_out);
  not not_47 (not_47_out, or_13_out);
  not not_48 (not_48_out, or_13_out);
  not not_49 (not_49_out, or_13_out);
  Divider_part #(.width(4)) divider_1 (.a(Dividend), .b(Divisor), .out(out_72), .rem(out_74));  // open: upper
  xor xor_23 (C0_2, xor_16_out, not_46_out);
  xor xor_24 (C1_2, xor_17_out, not_47_out);
  xor xor_25 (C2_2, xor_21_out, not_48_out);
  xor xor_26 (C3_2, xor_22_out, not_49_out);

  assign R3 = A3_2;

  // Notes on the sheet:
  //   Assignment 6
  //   4 Bit Signed Multiplier
  //   4 Bit Signed Divider
  //   4 Bit Multiplier
  //   4 Bit Unigned Divider
endmodule

module Divider (
  input  B3,
  input  A3,
  input  A2,
  input  A1,
  input  A0,
  input  B2,
  input  B1,
  input  B0,
  output D3,
  output D2,
  output D1,
  output D0,
  output R3,
  output R2,
  output R1,
  output R0
);

  wire and_2_out, and_3_out, and_4_out, and_5_out, and_6_out, and_7_out, and_8_out, and_9_out, and_10_out,
       and_11_out, and_12_out, and_13_out, and_14_out, and_15_out, and_16_out, and_17_out, and_18_out,
       and_19_out, and_20_out, and_21_out, and_22_out, and_23_out, and_24_out, and_25_out, and_26_out,
       and_27_out, and_28_out, and_29_out, and_30_out, not_1_out, not_2_out, not_3_out, not_4_out, not_5_out,
       not_6_out, not_7_out, not_8_out, not_9_out, not_10_out, not_11_out, not_12_out, not_13_out,
       not_14_out, not_15_out, not_16_out, not_17_out, not_18_out, not_19_out, not_20_out, not_21_out,
       not_22_out, not_23_out, not_24_out, not_25_out, not_26_out, not_27_out, not_28_out, not_29_out,
       not_30_out, not_31_out, not_32_out, not_33_out, not_34_out, not_35_out, not_36_out, not_37_out,
       not_38_out, not_39_out, not_40_out, not_41_out, not_42_out, not_43_out, not_44_out, not_45_out;

  not not_1 (not_1_out, B2);
  not not_2 (not_2_out, B1);
  not not_3 (not_3_out, B2);
  not not_4 (not_4_out, B1);
  not not_5 (not_5_out, B2);
  not not_6 (not_6_out, B0);
  not not_7 (not_7_out, B2);
  not not_8 (not_8_out, B2);
  not not_9 (not_9_out, B1);
  not not_10 (not_10_out, B2);
  not not_11 (not_11_out, B0);
  not not_12 (not_12_out, A2);
  not not_13 (not_13_out, B2);
  not not_14 (not_14_out, A1);
  not not_15 (not_15_out, B2);
  not not_16 (not_16_out, B1);
  not not_17 (not_17_out, B0);
  not not_18 (not_18_out, B1);
  not not_19 (not_19_out, B1);
  not not_20 (not_20_out, B0);
  not not_21 (not_21_out, A1);
  not not_22 (not_22_out, A0);
  not not_23 (not_23_out, A1);
  not not_24 (not_24_out, A0);
  not not_25 (not_25_out, A2);
  not not_26 (not_26_out, A0);
  not not_27 (not_27_out, A2);
  not not_28 (not_28_out, B1);
  not not_29 (not_29_out, B0);
  not not_30 (not_30_out, A0);
  not not_31 (not_31_out, B1);
  not not_32 (not_32_out, A1);
  not not_33 (not_33_out, B2);
  not not_34 (not_34_out, A2);
  not not_35 (not_35_out, A1);
  not not_36 (not_36_out, B0);
  not not_37 (not_37_out, A2);
  not not_38 (not_38_out, A1);
  not not_39 (not_39_out, B0);
  not not_40 (not_40_out, A1);
  not not_41 (not_41_out, A0);
  not not_42 (not_42_out, B2);
  not not_43 (not_43_out, A0);
  not not_44 (not_44_out, B1);
  not not_45 (not_45_out, B2);
  xor xor_1 (D3, A3, B3);
  and and_1 (D2, A2, not_1_out, not_2_out, B0);
  and and_2 (and_2_out, A1, not_3_out, not_4_out, B0);
  and and_3 (and_3_out, A2, not_5_out, B1, not_6_out);
  and and_4 (and_4_out, A2, A1, not_7_out, B1);
  and and_5 (and_5_out, A0, not_8_out, not_9_out, B0);
  and and_6 (and_6_out, A1, not_10_out, B1, not_11_out);
  and and_7 (and_7_out, not_12_out, A1, A0, not_13_out, B1);
  and and_8 (and_8_out, A2, not_14_out, not_15_out, B1, B0);
  and and_9 (and_9_out, A2, B2, not_16_out, not_17_out);
  and and_10 (and_10_out, A2, A0, B2, not_18_out);
  and and_11 (and_11_out, A2, A1, B2, not_19_out);
  and and_12 (and_12_out, A2, A1, B2, not_20_out);
  and and_13 (and_13_out, A2, A1, A0, B2);
  and and_14 (and_14_out, A2, not_21_out, not_22_out, B2, B0);
  and and_15 (and_15_out, A2, not_23_out, B2, B1);
  and and_16 (and_16_out, A2, not_24_out, B2, B1, B0);
  and and_17 (and_17_out, not_25_out, A1, not_26_out, B1, B0);
  and and_18 (and_18_out, not_27_out, A1, B2);
  and and_19 (and_19_out, A1, B2, not_28_out, not_29_out);
  and and_20 (and_20_out, A1, not_30_out, B2, B1, B0);
  and and_21 (and_21_out, A1, A0, B2, not_31_out);
  and and_22 (and_22_out, A2, not_32_out, A0, not_33_out, B1, B0);
  and and_23 (and_23_out, not_34_out, not_35_out, A0, B1);
  and and_24 (and_24_out, A0, B1, not_36_out);
  and and_25 (and_25_out, not_37_out, A0, B2);
  and and_26 (and_26_out, not_38_out, A0, B2);
  and and_27 (and_27_out, A0, B2, not_39_out);
  and and_28 (and_28_out, A2, not_40_out, not_41_out, not_42_out, B1, B0);
  and and_29 (and_29_out, A2, A1, not_43_out, B2, not_44_out, B0);
  and and_30 (and_30_out, A2, A1, A0, not_45_out, B1);
  or or_1 (D1, and_2_out, and_3_out, and_4_out);
  or or_2 (D0, and_5_out, and_6_out, and_7_out, and_8_out, and_9_out, and_10_out, and_11_out, and_12_out, and_13_out);
  or or_3 (R2, and_14_out, and_15_out, and_16_out);
  or or_4 (R1, and_17_out, and_18_out, and_19_out, and_20_out, and_21_out, and_22_out);
  or or_5 (R0, and_23_out, and_24_out, and_25_out, and_26_out, and_27_out, and_28_out, and_29_out, and_30_out);

  assign R3 = A3;
endmodule
