// Logisim project Assignment_7.circ as structural Verilog: 1 circuit, main circuit main
module main (
  input  ROM_Chip_Select,
  input  RAM_Load,
  input  RAM_Chip_Select,
  input  in_4
);

  wire Counter_Clear_out, System_Clock_out;
  wire [6:0] ram_1_data;
  wire [7:0] counter_1_q, rom_1_data;

  Clock System_Clock (.out(System_Clock_out));
  Button Counter_Clear (.out(Counter_Clear_out));
  Counter #(.max('h9)) counter_1 (
    .Q(counter_1_q), .clk(System_Clock_out), .clr(Counter_Clear_out));  // open: load, D, count, carry
  ROM rom_1 (.addr(counter_1_q), .data(rom_1_data), .sel(ROM_Chip_Select));
  RAM #(.dataWidth(7)) ram_1 (
    .addr(rom_1_data), .data(ram_1_data), .sel(RAM_Chip_Select), .clk(System_Clock_out), .ld(RAM_Load));  // open: clr
  _7_Segment_Display u_7_segment_display_1 (
    .g(ram_1_data[6]), .f(ram_1_data[5]), .a(ram_1_data[0]), .b(ram_1_data[1]), .e(ram_1_data[4]),
    .d(ram_1_data[3]), .c(ram_1_data[2]));  // open: dp

  // Notes on the sheet:
  //   Assignment 7- Basics of RAM and ROM
  //   contents of rom_1 (hex, n*v repeats v):
  //   0 1 2 3 4 5 6 7 8 9
  //   Codes: 0 - 3f  1-06  2-5b  3-4f  4-66  5-6d  6-7d  7-07  8-7f  9-6f
endmodule
