// Logisim project Assignment_8.circ as structural Verilog: 1 circuit, main circuit main
module main (
  input  S1,
  input  S0,
  input  ENABLE,
  input  A1,
  input  A0,
  input  B1,
  input  B0,
  input  B1_2,
  input  B0_2,
  input  A1_2,
  input  A0_2,
  input  in_12,
  input  in_13,
  input  in_14,
  input  in_15,
  input  in_16,
  input  in_17,
  input  in_18,
  input  in_19,
  input  in_20,
  output out_21,
  output out_22,
  output out_23,
  output out_24,
  output G,
  output E,
  output L,
  output C0,
  output C1,
  output C2,
  output C3,
  output C0_2,
  output C1_2,
  output C2_2,
  output C3_2,
  output C4
);

  wire and_2_out, and_3_out, and_4_out, and_5_out, and_6_out, and_7_out, and_8_out, and_9_out, and_10_out,
       and_11_out, and_12_out, and_13_out, and_14_out, and_19_out, and_20_out, and_21_out, and_22_out,
       and_23_out, and_24_out, and_25_out, and_26_out, and_27_out, D_out, not_1_out, not_2_out, not_3_out,
       not_4_out, not_5_out, not_6_out, not_7_out, not_8_out, not_9_out, not_10_out, not_11_out, not_12_out,
       not_13_out, not_14_out, not_15_out, not_16_out, not_17_out, not_18_out, or_4_out, or_5_out, or_6_out,
       xor_1_out, xor_2_out, xor_3_out, xor_4_out;

  Button D (.out(D_out));
  not not_1 (not_1_out, S1);
  not not_2 (not_2_out, S0);
  not not_3 (not_3_out, B0);
  not not_4 (not_4_out, B1);
  not not_5 (not_5_out, A1);
  not not_6 (not_6_out, A0);
  not not_7 (not_7_out, B1);
  not not_8 (not_8_out, B0);
  not not_9 (not_9_out, A1);
  not not_10 (not_10_out, B1);
  not not_11 (not_11_out, A0);
  not not_12 (not_12_out, B0);
  not not_13 (not_13_out, A1);
  not not_14 (not_14_out, A0);
  not not_15 (not_15_out, A1);
  not not_16 (not_16_out, A0);
  not not_17 (not_17_out, A1);
  not not_18 (not_18_out, A0);
  and and_1 (C0, A0_2, B0_2);
  and and_2 (and_2_out, A1_2, B0_2);
  and and_3 (and_3_out, B1_2, A0_2);
  and and_4 (and_4_out, B1_2, A1_2);
  and and_5 (and_5_out, A0, not_3_out);
  or or_1 (G, and_5_out, and_6_out);
  and and_6 (and_6_out, A1, not_4_out);
  and and_7 (and_7_out, not_5_out, not_6_out, not_7_out, not_8_out);
  and and_8 (and_8_out, not_9_out, A0, not_10_out, B0);
  and and_9 (and_9_out, A1, not_11_out, B1, not_12_out);
  and and_10 (and_10_out, A1, A0, B1, B0);
  and and_11 (and_11_out, not_13_out, not_14_out, B0);
  and and_12 (and_12_out, not_15_out, not_16_out, B1);
  and and_13 (and_13_out, not_17_out, B1, B0);
  and and_14 (and_14_out, not_18_out, B1, B0);
  and and_15 (out_21, not_2_out, not_1_out, D_out, ENABLE);
  and and_16 (out_22, S0, not_1_out, D_out, ENABLE);
  and and_17 (out_23, not_2_out, S1, D_out, ENABLE);
  and and_18 (out_24, S0, S1, D_out, ENABLE);
  or or_2 (E, and_7_out, and_8_out, and_9_out, and_10_out);
  or or_3 (L, and_11_out, and_12_out, and_13_out, and_14_out);
  xor xor_1 (xor_1_out, in_12, in_20);
  xor xor_2 (xor_2_out, or_4_out, in_19);
  xor xor_3 (xor_3_out, or_5_out, in_18);
  and and_19 (and_19_out, xor_1_out, in_16);
  and and_20 (and_20_out, in_20, in_12);
  and and_21 (and_21_out, xor_2_out, in_15);
  and and_22 (and_22_out, in_19, or_4_out);
  and and_23 (and_23_out, xor_3_out, in_14);
  and and_24 (and_24_out, in_18, or_5_out);
  xor xor_4 (xor_4_out, or_6_out, in_17);
  and and_25 (and_25_out, xor_4_out, in_13);
  and and_26 (and_26_out, in_17, or_6_out);
  xor xor_5 (C1, and_2_out, and_3_out);
  and and_27 (and_27_out, and_2_out, and_3_out);
  xor xor_6 (C2, and_27_out, and_4_out);
  and and_28 (C3, and_27_out, and_4_out);
  xor xor_7 (C0_2, xor_1_out, in_16);
  or or_4 (or_4_out, and_19_out, and_20_out);
  xor xor_8 (C1_2, xor_2_out, in_15);
  or or_5 (or_5_out, and_21_out, and_22_out);
  xor xor_9 (C2_2, xor_3_out, in_14);
  or or_6 (or_6_out, and_23_out, and_24_out);
  xor xor_10 (C3_2, xor_4_out, in_13);
  or or_7 (C4, and_25_out, and_26_out);

  // Notes on the sheet:
  //   1:4 Demultiplexer
  //   2 bit Magnitude Comparator
  //   2-Bit Multiplier
  //   4-Bit Binary Adder
endmodule
