// Logisim project Assignment_9.circ as structural Verilog: 1 circuit, main circuit main
module main (
  input  in_1,
  input  _1,
  output Odd_Parity_Checker,
  output Even_Parity_Checker
);

  wire clock_1_out, xor_1_out, xor_2_out, xor_3_out, xor_4_out, xor_5_out, xor_6_out;
  wire [6:0] rom_1_data, rom_2_data, rom_3_data, rom_4_data;
  wire [7:0] counter_1_q, register_1_q;

  Counter counter_1 (.count(in_1), .Q(counter_1_q), .clk(clock_1_out));  // open: load, D, carry, clr
  Register register_1 (.D(counter_1_q), .en(in_1), .Q(register_1_q), .clk(clock_1_out));  // open: clr
  Clock clock_1 (.out(clock_1_out));
  xor xor_1 (xor_1_out, register_1_q[0], register_1_q[1]);
  xor xor_2 (xor_2_out, register_1_q[2], register_1_q[3]);
  xor xor_3 (xor_3_out, register_1_q[4], register_1_q[5]);
  xor xor_4 (xor_4_out, register_1_q[6], register_1_q[7]);
  ROM #(.addrWidth(2), .dataWidth(7)) rom_1 (.addr(register_1_q[1:0]), .data(rom_1_data));  // open: sel
  ROM #(.addrWidth(2), .dataWidth(7)) rom_2 (.addr(register_1_q[3:2]), .data(rom_2_data));  // open: sel
  ROM #(.addrWidth(2), .dataWidth(7)) rom_3 (.addr(register_1_q[5:4]), .data(rom_3_data));  // open: sel
  ROM #(.addrWidth(2), .dataWidth(7)) rom_4 (.addr(register_1_q[7:6]), .data(rom_4_data));  // open: sel
  xor xor_5 (xor_5_out, xor_1_out, xor_2_out);
  xor xor_6 (xor_6_out, xor_3_out, xor_4_out);
  xor xor_7 (Odd_Parity_Checker, xor_5_out, xor_6_out);
  xor xor_8 (Even_Parity_Checker, _1, Odd_Parity_Checker);
  _7_Segment_Display u_7_segment_display_1 (
    .g(rom_1_data[6]), .f(rom_1_data[5]), .a(rom_1_data[0]), .b(rom_1_data[1]), .e(rom_1_data[4]),
    .d(rom_1_data[3]), .c(rom_1_data[2]));  // open: dp
  _7_Segment_Display u_7_segment_display_2 (
    .g(rom_2_data[6]), .f(rom_2_data[5]), .a(rom_2_data[0]), .b(rom_2_data[1]), .e(rom_2_data[4]),
    .d(rom_2_data[3]), .c(rom_2_data[2]));  // open: dp
  _7_Segment_Display u_7_segment_display_3 (
    .g(rom_3_data[6]), .f(rom_3_data[5]), .a(rom_3_data[0]), .b(rom_3_data[1]), .e(rom_3_data[4]),
    .d(rom_3_data[3]), .c(rom_3_data[2]));  // open: dp
  _7_Segment_Display u_7_segment_display_4 (
    .g(rom_4_data[6]), .f(rom_4_data[5]), .a(rom_4_data[0]), .b(rom_4_data[1]), .e(rom_4_data[4]),
    .d(rom_4_data[3]), .c(rom_4_data[2]));  // open: dp

  // Notes on the sheet:
  //   Assignment 9
  //   OpCode Memory
  //   Operand 1 Address Decoder
  //   Operand 2 Address Decoder
  //   Offset to Seven Segment Decoder
  //   contents of rom_1 (hex, n*v repeats v):
  //   3f 6 5b 4f
  //   contents of rom_2 (hex, n*v repeats v):
  //   3f 6 5b 4f
  //   contents of rom_3 (hex, n*v repeats v):
  //   3f 6 5b 4f
  //   contents of rom_4 (hex, n*v repeats v):
  //   3f 6 5b 4f
  //   Opcode Value
  //   Operand 1 Address Value
  //   Operand 2 Address Value
  //   Offset Value
endmodule
